# Fritzing sketch free_IoT_Services_Project_II (saved by Fritzing 0.9.3b)
breadboards: 4

parts:
  e-radionica1 = TCS230 Color Sensor [part_number=101209]
  LED1 = smd LED [color="Red (633nm)" package="0603 [SMD]"]
  U1 = NodeMCU V1.0

nets:
  GND: e-radionica1.Gnd, LED1.anode, U1.GND
  N1: e-radionica1.S1, U1.D3
  N2: e-radionica1.S0, U1.D2
  N3: e-radionica1.S3, U1.D5
  N4: e-radionica1.S2, U1.D4
  N5: e-radionica1.Out, U1.D6
  VCC: e-radionica1.Vcc, U1.3V3
  N6: LED1.cathode, U1.D1

notes:
  TCS3200 Color Sensor
  Control Led
  NodeMCU [ESP-12E]

custom parts:
  TCS230 Color Sensor: TCS230
  NodeMCU V1.0: ESP8266 based NodeMCU
